# Fritzing sketch input_opto_isolators (saved by Fritzing 0.8.5b)
circuit board: 3.8cm x 3.3cm
breadboards: 1

parts:
  U1 = Optocoupler [package=THT]
  U2 = Optocoupler [package=THT]
  U3 = Optocoupler [package=THT]
  U4 = Optocoupler [package=THT]
  R1 = Resistor [tolerance=±5% resistance=330 package=THT]
  R2 = Resistor [tolerance=±5% resistance=330 package=THT]
  R3 = Resistor [tolerance=±5% resistance=330 package=THT]
  R4 = Resistor [tolerance=±5% resistance=330 package=THT]
  J2 = female pin header, 6 pins [form="♀ (female)"]
  D4 = Rectifier Diode [part_number=1N4001 package="300 mil [THT]"]
  D3 = Rectifier Diode [part_number=1N4001 package="300 mil [THT]"]
  D2 = Rectifier Diode [part_number=1N4001 package="300 mil [THT]"]
  D1 = Rectifier Diode [part_number=1N4001 package="300 mil [THT]"]
  J1 = screw terminal, 5 pins

nets:
  N1: U1.Pin_1, R1.Pin_1
  N2: U1.Pin_2, U2.Pin_2, U3.Pin_2, U4.Pin_2, D4.anode, D3.anode, D2.anode, D1.anode, J1.pin1
  N3: U1.Pin_4, U2.Pin_4, U3.Pin_4, U4.Pin_4, J2.pin6
  N4: U1.Pin_5, J2.pin2
  N5: U2.Pin_1, R2.Pin_1
  N6: U2.Pin_5, J2.pin3
  N7: U3.Pin_1, R3.Pin_1
  N8: U3.Pin_5, J2.pin4
  N9: U4.Pin_1, R4.Pin_1
  N10: U4.Pin_5, J2.pin5
  N11: R1.Pin_0, D1.cathode, J1.pin5
  N12: R2.Pin_0, D2.cathode, J1.pin4
  N13: R3.Pin_0, D3.cathode, J1.pin3
  N14: R4.Pin_0, D4.cathode, J1.pin2
