# Fritzing sketch mega_2560_shield (saved by Fritzing 0.8.5b)
circuit board: 10.16cm x 5.36194cm
breadboards: 1

parts:
  Part1 = Arduino Mega 2560 (Rev3)
  J12 = male pin header, 4 pins [form="♂ (male)"]
  J13 = male pin header, 2 pins [form="♂ (male)"]
  J14 = male pin header, 3 pins [form="♂ (male)"]
  C3 = Electrolytic Capacitor [capacitance=10µF voltage=50V package="100 mil [THT, electrolytic]"]
  U3 = Optocoupler [package=THT]
  R3 = Resistor [tolerance=±5% resistance=330 package=THT]
  D14 = Rectifier Diode [part_number=1N4001 package="300 mil [THT]"]
  R4 = Resistor [tolerance=±5% resistance=100k package=THT]
  J15 = male pin header, 2 pins [form="♂ (male)"]
  J16 = male pin header, 2 pins [form="♂ (male)"]
  J17 = male pin header, 2 pins [form="♂ (male)"]
  U4 = Optocoupler [package=THT]
  R5 = Resistor [tolerance=±5% resistance=330 package=THT]
  D15 = Rectifier Diode [part_number=1N4001 package="300 mil [THT]"]
  J18 = male pin header, 3 pins [form="♂ (male)"]
  R6 = Resistor [tolerance=±5% resistance=100k package=THT]
  C4 = Ceramic Capacitor [capacitance=100nF package="100 mil [THT, multilayer]"]
  J20 = male alternating pin header, 3 pins [form="♂ (male)"]
  R14 = Resistor [tolerance=±5% resistance=220 package=THT]
  R15 = Resistor [tolerance=±5% resistance=220 package=THT]
  R17 = Resistor [tolerance=±5% resistance=220 package=THT]
  R18 = Resistor [tolerance=±5% resistance=220 package=THT]
  J21 = female pin header, 8 pins [form="♀ (female)"]
  R21 = Resistor [tolerance=±5% resistance=100k package=THT]
  R27 = Resistor [tolerance=±5% resistance=10k package=THT]
  R26 = Resistor [tolerance=±5% resistance=10k package=THT]
  R25 = Resistor [tolerance=±5% resistance=10k package=THT]
  R24 = Resistor [tolerance=±5% resistance=10k package=THT]
  R23 = Resistor [tolerance=±5% resistance=10k package=THT]
  R20 = Resistor [tolerance=±5% resistance=10k package=THT]
  R22 = Resistor [tolerance=±5% resistance=10k package=THT]
  R16 = Resistor [tolerance=±5% resistance=220 package=THT]
  R19 = Resistor [tolerance=±5% resistance=220 package=THT]
  R28 = Resistor [tolerance=±5% resistance=10k package=THT]
  J22 = male pin header, 8 pins [form="♂ (male)"]
  J19 = male pin header, 8 pins [form="♂ (male)"]
  J23 = male pin header, 8 pins [form="♂ (male)"]

nets (from the schematic view):
  N1: Part1.A0, R22.Pin_1
  N2: Part1.A1, R23.Pin_0
  N3: Part1.A2, R24.Pin_0
  N4: Part1.A3, R25.Pin_0
  N5: Part1.A4, R26.Pin_0
  N6: Part1.A5, R27.Pin_0
  N7: Part1.A6, R28.Pin_0
  N8: Part1.D21/SCL, J19.pin8
  N9: Part1.D20/SDA, J19.pin7
  N10: Part1.D19/RX1, J19.pin6
  N11: Part1.D18/TX1, J19.pin5
  N12: Part1.D17_PWM/RX2, J19.pin4
  N13: Part1.D16_PWM/TX2, J19.pin3
  N14: Part1.D15/RX3, J19.pin2
  N15: Part1.D14/TX3, J19.pin1
  GND: Part1.GND, J12.pin4, J13.pin1, J14.pin1, C3.-, U3.Pin_2, U3.Pin_4, D14.anode, J15.pin1, J16.pin1, J17.pin1, U4.Pin_2, U4.Pin_4, D15.anode, J18.pin1, C4.0, R20.Pin_0
  N16: Part1.D13_PWM, J20.pin1
  N17: Part1.D12_PWM, J20.pin2
  N18: Part1.D11_PWM, J20.pin3
  N19: Part1.D10_PWM, J12.pin1
  N20: Part1.D9_PWM, J12.pin2
  N21: Part1.D8_PWM, J12.pin3
  N22: Part1.5V, R4.Pin_1, R6.Pin_1
  N23: Part1.VIN, J13.pin2, J14.pin3, C3.+, J18.pin3, C4.1
  N24: Part1.D2_PWM, U3.Pin_5, R4.Pin_0
  N25: Part1.D3_PWM, U4.Pin_5, R6.Pin_0
  N26: Part1.D5_PWM, J16.pin2
  N27: Part1.D6_PWM, J15.pin2
  N28: Part1.D7_PWM, J17.pin2
  N29: Part1.D22, J22.pin1
  N30: Part1.D24, J22.pin2
  N31: Part1.D26, J22.pin3
  N32: Part1.D28, J22.pin4
  N33: Part1.D30, J22.pin5
  N34: Part1.D32, J22.pin6
  N35: Part1.D34, J22.pin7
  N36: Part1.D36, J22.pin8
  N37: Part1.D38, J23.pin1
  N38: Part1.D40, J23.pin2
  N39: Part1.D42, J23.pin3
  N40: Part1.D44, J23.pin4
  N41: Part1.D46, J23.pin5
  N42: Part1.D48, J23.pin6
  N43: Part1.D50, J23.pin7
  N44: Part1.D52, J23.pin8
  N45: J14.pin2, R3.Pin_0
  N46: U3.Pin_1, R3.Pin_1, D14.cathode
  N47: U4.Pin_1, R5.Pin_1, D15.cathode
  N48: R5.Pin_0, J18.pin2
  N49: R14.Pin_0, R15.Pin_0, R17.Pin_0, R18.Pin_0, J21.pin8, R16.Pin_0, R19.Pin_0
  N50: R14.Pin_1, J21.pin2, R23.Pin_1
  N51: R15.Pin_1, J21.pin3, R24.Pin_1
  N52: R17.Pin_1, J21.pin5, R26.Pin_1
  N53: R18.Pin_1, J21.pin6, R27.Pin_1
  N54: J21.pin1, R21.Pin_0
  N55: J21.pin4, R25.Pin_1, R16.Pin_1
  N56: J21.pin7, R19.Pin_1, R28.Pin_1
  N57: R21.Pin_1, R20.Pin_1, R22.Pin_0
