# Fritzing sketch gauges_sensor_shield (saved by Fritzing 0.8.5b)
circuit board: 6.9215cm x 5.33756cm

parts:
  R1 = Resistor [tolerance=±5% resistance=100k package=THT]
  R2 = Resistor [tolerance=±5% resistance=10k package=THT]
  R3 = Resistor [tolerance=±5% resistance=10k package=THT]
  Part1 = Arduino Uno (Rev3)
  R4 = Resistor [tolerance=±5% resistance=10k package=THT]
  R5 = Resistor [tolerance=±5% resistance=220 package=THT]
  R6 = Resistor [tolerance=±5% resistance=10k package=THT]
  R7 = Resistor [tolerance=±5% resistance=220 package=THT]
  J1 = female pin header, 8 pins [form="♀ (female)"]
  R8 = Resistor [tolerance=±5% resistance=10k package=THT]
  R9 = Resistor [tolerance=±5% resistance=220 package=THT]
  R10 = Resistor [tolerance=±5% resistance=10k package=THT]
  R11 = Resistor [tolerance=±5% resistance=220 package=THT]
  R12 = Resistor [tolerance=±5% resistance=10k package=THT]
  R13 = Resistor [tolerance=±5% resistance=220 package=THT]
  J2 = female pin header, 4 pins [form="♀ (female)"]
  D1 = Rectifier Diode [part_number=1N4001 package="300 mil [THT]"]

nets:
  N1: R1.Pin_0, J1.pin8
  N2: R1.Pin_1, R2.Pin_1, R3.Pin_0
  N3: R2.Pin_0, Part1.GND, J2.pin1
  N4: R3.Pin_1, Part1.A0
  N5: Part1.A1, R4.Pin_0
  N6: Part1.A2, R6.Pin_0
  N7: Part1.A3, R8.Pin_0
  N8: Part1.A4/SDA, R10.Pin_0
  N9: Part1.A5/SCL, R12.Pin_0
  N10: Part1.D11_PWM/MOSI, J2.pin3
  N11: Part1.D12/MISO, J2.pin2
  N12: Part1.D3_PWM, J2.pin4
  N13: Part1.VIN, D1.cathode
  N14: R4.Pin_1, R5.Pin_1, J1.pin7
  N15: R5.Pin_0, R7.Pin_0, J1.pin2, R9.Pin_0, R11.Pin_0, R13.Pin_0
  N16: R6.Pin_1, R7.Pin_1, J1.pin6
  N17: J1.pin1, D1.anode
  N18: J1.pin3, R12.Pin_1, R13.Pin_1
  N19: J1.pin4, R10.Pin_1, R11.Pin_1
  N20: J1.pin5, R8.Pin_1, R9.Pin_1
