# Fritzing sketch general_input (saved by Fritzing 0.8.5b)
circuit board: 8.4cm x 6.8cm
breadboards: 1

parts:
  J3 = screw terminal, 10 pins
  J2 = male pin header, 10 pins [form="♂ (male)"]
  J4 = male pin header, 3 pins [form="♂ (male)"]

nets:
  N1: J3.pin2, J4.pin3
  N2: J3.pin5, J2.pin6
  N3: J3.pin6, J2.pin5
  N4: J3.pin7, J2.pin4
  N5: J3.pin8, J2.pin3
  N6: J3.pin9, J2.pin2
  N7: J3.pin10, J2.pin1
  N8: J2.pin7, J4.pin2
