# Fritzing sketch mega_2560_shield_simplified (saved by Fritzing 0.8.5b)
circuit board: 10.16cm x 5.36194cm
breadboards: 1

parts:
  Part1 = Arduino Mega 2560 (Rev3)
  U3 = Optocoupler [package=THT]
  R3 = Resistor [tolerance=±5% resistance=330 package=THT]
  D14 = Rectifier Diode [part_number=1N4001 package="300 mil [THT]"]
  R4 = Resistor [tolerance=±5% resistance=100k package=THT]
  U4 = Optocoupler [package=THT]
  R5 = Resistor [tolerance=±5% resistance=330 package=THT]
  D15 = Rectifier Diode [part_number=1N4001 package="300 mil [THT]"]
  R6 = Resistor [tolerance=±5% resistance=100k package=THT]
  C4 = Ceramic Capacitor [capacitance=100nF package="100 mil [THT, multilayer]"]
  R14 = Resistor [tolerance=±5% resistance=220 package=THT]
  R15 = Resistor [tolerance=±5% resistance=220 package=THT]
  R21 = Resistor [tolerance=±5% resistance=100k package=THT]
  R25 = Resistor [tolerance=±5% resistance=10k package=THT]
  R24 = Resistor [tolerance=±5% resistance=10k package=THT]
  R23 = Resistor [tolerance=±5% resistance=10k package=THT]
  R20 = Resistor [tolerance=±5% resistance=10k package=THT]
  R22 = Resistor [tolerance=±5% resistance=10k package=THT]
  R16 = Resistor [tolerance=±5% resistance=220 package=THT]
  J3 = male pin header, 4 pins [form="♂ (male)"]
  J13 = male pin header, 2 pins [form="♂ (male)"]
  J2 = male pin header, 3 pins [form="♂ (male)"]
  J1 = male pin header, 3 pins [form="♂ (male)"]
  C3 = Electrolytic Capacitor [capacitance=10µF voltage=50V package="100 mil [THT, electrolytic]"]
  J6 = shrouded pin header, 10 pins [form="♂ (shrouded male)"]
  J7 = shrouded pin header, 10 pins [form="♂ (shrouded male)"]
  J8 = shrouded pin header, 10 pins [form="♂ (shrouded male)"]
  J4 = male pin header, 3 pins [form="♂ (male)"]
  J5 = male pin header, 3 pins [form="♂ (male)"]

nets (from the schematic view):
  N1: Part1.A0, R22.Pin_1
  N2: Part1.A1, R23.Pin_0
  N3: Part1.A2, R24.Pin_0
  N4: Part1.A3, R25.Pin_0
  GND: Part1.A4, Part1.A5, Part1.A6, Part1.A7, Part1.GND, U3.Pin_2, U3.Pin_4, D14.anode, U4.Pin_2, U4.Pin_4, D15.anode, C4.0, J3.pin4, J13.pin1, J2.pin1, J1.pin1, C3.-, J6.pin1, J6.pin2, J6.pin3, J6.pin4, J7.pin1, J7.pin2, J7.pin3, J7.pin4, J5.pin2
  N5: Part1.D16_PWM/TX2, J6.pin8
  N6: Part1.D15/RX3, J6.pin9
  N7: Part1.D14/TX3, J6.pin10
  N8: Part1.D10_PWM, J3.pin1
  N9: Part1.D9_PWM, J3.pin2
  N10: Part1.D8_PWM, J3.pin3
  N11: Part1.5V, R4.Pin_1, R6.Pin_1
  N12: Part1.VIN, C4.1, J13.pin2, J2.pin3, J1.pin3, C3.+
  N13: Part1.D2_PWM, U3.Pin_5, R4.Pin_0
  N14: Part1.D3_PWM, U4.Pin_5, R6.Pin_0
  N15: Part1.D5_PWM, J4.pin3
  N16: Part1.D6_PWM, J4.pin2
  N17: Part1.D7_PWM, J4.pin1
  N18: Part1.D24, J7.pin10
  N19: Part1.D28, J7.pin9
  N20: Part1.D30, J7.pin8
  N21: Part1.D32, J7.pin7
  N22: Part1.D34, J7.pin6
  N23: Part1.D36, J7.pin5
  N24: U3.Pin_1, R3.Pin_1, D14.cathode
  N25: R3.Pin_0, J1.pin2
  N26: U4.Pin_1, R5.Pin_1, D15.cathode
  N27: R5.Pin_0, J2.pin2
  N28: R14.Pin_0, R15.Pin_0, R16.Pin_0, J8.pin10
  N29: R14.Pin_1, R23.Pin_1, J8.pin6
  N30: R15.Pin_1, R24.Pin_1, J8.pin7
  N31: R21.Pin_0, J8.pin5
  N32: R21.Pin_1, R20.Pin_1, R22.Pin_0
  N33: R25.Pin_1, R16.Pin_1, J8.pin8
  N34: R20.Pin_0, J8.pin1, J8.pin2, J8.pin3, J8.pin4
  N35: J5.pin1, J5.pin3
