# Fritzing sketch powersupply (saved by Fritzing 0.8.5b)
circuit board: 6.8cm x 4.4cm
perfboards: 1

parts:
  C1 = Electrolytic Capacitor [capacitance=10µF voltage=50V package="100 mil [THT, electrolytic]"]
  C2 = Electrolytic Capacitor [capacitance=10µF voltage=50V package="100 mil [THT, electrolytic]"]
  C3 = Ceramic Capacitor [capacitance=0.1µF package="100 mil [THT, multilayer]"]
  C4 = Ceramic Capacitor [capacitance=0.1µF package="100 mil [THT, multilayer]"]
  C5 = Ceramic Capacitor [capacitance=0.1µF package="100 mil [THT, multilayer]"]
  C6 = Ceramic Capacitor [capacitance=0.1µF package="100 mil [THT, multilayer]"]
  C8 = Ceramic Capacitor [capacitance=0.1µF package="100 mil [THT, multilayer]"]
  C9 = Ceramic Capacitor [capacitance=0.1µF package="100 mil [THT, multilayer]"]
  U1 = Voltage Regulator - 5V [package="TO220 [THT]"]
  U4 = Voltage Regulator - 9V [package="TO220 [THT]"]
  U3 = Voltage Regulator - 5V [package="TO220 [THT]"]
  J9 = male pin header, 2 pins [form="♂ (male)"]
  U5 = Voltage Regulator - 9V [package="TO220 [THT]"]
  C10 = Electrolytic Capacitor [capacitance=10µF voltage=50V package="100 mil [THT, electrolytic]"]
  C11 = Ceramic Capacitor [capacitance=0.1µF package="100 mil [THT, multilayer]"]
  C12 = Ceramic Capacitor [capacitance=0.1µF package="100 mil [THT, multilayer]"]
  D1 = Rectifier Diode [part_number=1N4001 package="300 mil [THT]"]
  D2 = Rectifier Diode [part_number=1N4001 package="300 mil [THT]"]
  J10 = male pin header, 2 pins [form="♂ (male)"]
  J6 = male pin header, 2 pins [form="♂ (male)"]
  J7 = male pin header, 2 pins [form="♂ (male)"]
  J8 = male pin header, 2 pins [form="♂ (male)"]
  J2 = screw terminal, 4 pins

nets:
  GND: C1.-, C2.-, C3.0, C4.0, C5.0, C6.0, C8.0, C9.0, U1.GND, U4.GND, U3.GND, J9.pin1, U5.GND, C10.-, C11.0, C12.0, J10.pin2, J6.pin2, J7.pin2, J8.pin2, J2.pin1, J2.pin3
  N1: C1.+, C3.1, C9.1, U1.input_voltage, U3.input_voltage, J9.pin2, U5.input_voltage, C10.+, C11.1, D2.cathode
  N2: C2.+, C5.1, U4.input_voltage, D1.cathode, D2.anode, J2.pin2
  N3: C4.1, U1.output_voltage, J7.pin1
  N4: C6.1, U4.output_voltage, J6.pin1
  N5: C8.1, U3.output_voltage, J8.pin1
  N6: U5.output_voltage, C12.1, J10.pin1
  N7: D1.anode, J2.pin4

custom parts:
  Voltage Regulator - 9V: 9V DC Voltage Regulator
