# Fritzing sketch gauges_arduino_nano_display_shield (saved by Fritzing 0.8.5b)
circuit board: 11.5cm x 9.5cm
breadboards: 1

parts:
  Part2 = Arduino Nano (Rev3.0)
  U1 = Voltage Regulator - 5V [package="TO220 [THT]"]
  J1 = female pin header, 2 pins [form="♀ (female)"]
  J2 = female pin header, 2 pins [form="♀ (female)"]
  J3 = female pin header, 2 pins [form="♀ (female)"]
  J4 = female pin header, 2 pins [form="♀ (female)"]
  J5 = female pin header, 2 pins [form="♀ (female)"]
  J6 = female pin header, 2 pins [form="♀ (female)"]
  J7 = female pin header, 2 pins [form="♀ (female)"]
  J8 = female pin header, 2 pins [form="♀ (female)"]
  C2 = Electrolytic Capacitor [capacitance=1µF package="100 mil [THT, electrolytic]"]
  C1 = Ceramic Capacitor [capacitance=100nF package="100 mil [THT, multilayer]"]

nets:
  GND: Part2.GND, U1.GND, J5.pin2, J6.pin2, J7.pin2, J8.pin2, C2.-, C1.0
  N1: Part2.D6, J4.pin1
  N2: Part2.D7, J1.pin1
  N3: Part2.D8, J3.pin1
  N4: Part2.D9, J2.pin1
  N5: Part2.VIN, U1.input_voltage
  N6: U1.output_voltage, J5.pin1, J6.pin1, J7.pin1, J8.pin1, C2.+, C1.1
