# Fritzing sketch speedo_arduino_nano_display_shield (saved by Fritzing 0.8.5b)
circuit board: 11.5cm x 7.5cm
breadboards: 1

parts:
  Part2 = Arduino Nano (Rev3.0)
  U1 = Voltage Regulator - 5V [package="TO220 [THT]"]
  J1 = male pin header, 3 pins [form="♂ (male)"]
  J2 = male pin header, 3 pins [form="♂ (male)"]
  J3 = male pin header, 4 pins [form="♂ (male)"]

nets:
  GND: Part2.GND, U1.GND, J1.pin2, J2.pin3, J3.pin2
  N1: Part2.D7, J1.pin3
  N2: Part2.D8, J3.pin4
  N3: Part2.D9, J2.pin2
  N4: Part2.VIN, U1.input_voltage
  N5: U1.output_voltage, J1.pin1, J2.pin1, J3.pin1
