# Fritzing sketch speedo_arduino_nano_input_shield (saved by Fritzing 0.8.5b)
circuit board: 10cm x 6.5cm
breadboards: 1

parts:
  J5 = male pin header, 2 pins [form="♂ (male)"]
  J6 = male pin header, 3 pins [form="♂ (male)"]
  C1 = Electrolytic Capacitor [capacitance=10µF voltage=50V package="100 mil [THT, electrolytic]"]
  C2 = Ceramic Capacitor [capacitance=100nF package="100 mil [THT, multilayer]"]
  U2 = Optocoupler [package=THT]
  R1 = Resistor [tolerance=±5% resistance=330 package=THT]
  D13 = Rectifier Diode [part_number=1N4001 package="300 mil [THT]"]
  J7 = male pin header, 2 pins [form="♂ (male)"]
  J8 = male pin header, 2 pins [form="♂ (male)"]
  J9 = male pin header, 4 pins [form="♂ (male)"]
  J10 = female pin header, 3 pins [form="♀ (female)"]
  Part1 = Arduino Nano (Rev3.0)
  U3 = Optocoupler [package=THT]
  R2 = Resistor [tolerance=±5% resistance=330 package=THT]
  D14 = Rectifier Diode [part_number=1N4001 package="300 mil [THT]"]
  U4 = Optocoupler [package=THT]
  R3 = Resistor [tolerance=±5% resistance=330 package=THT]
  D15 = Rectifier Diode [part_number=1N4001 package="300 mil [THT]"]
  U5 = Optocoupler [package=THT]
  R4 = Resistor [tolerance=±5% resistance=330 package=THT]
  D16 = Rectifier Diode [part_number=1N4001 package="300 mil [THT]"]
  U6 = Voltage Regulator - 9V [package="TO220 [THT]"]
  J11 = male pin header, 4 pins [form="♂ (male)"]
  C3 = Electrolytic Capacitor [capacitance=10µF voltage=50V package="100 mil [THT, electrolytic]"]
  J12 = female pin header, 3 pins [form="♀ (female)"]

nets (from the schematic view):
  GND: J5.pin1, J6.pin1, C1.-, C2.0, U2.Pin_2, U2.Pin_4, D13.anode, J7.pin1, J8.pin1, J9.pin1, Part1.GND, U3.Pin_2, U3.Pin_4, D14.anode, U4.Pin_2, U4.Pin_4, D15.anode, U5.Pin_2, U5.Pin_4, D16.anode, U6.GND, J11.pin1, C3.-
  N1: J5.pin2, U6.input_voltage, C3.+
  N2: J6.pin2, R1.Pin_0
  N3: J6.pin3, C1.+, C2.1, Part1.VIN, U6.output_voltage
  N4: U2.Pin_1, R1.Pin_1, D13.cathode
  N5: U2.Pin_5, Part1.D2
  N6: J7.pin2, Part1.D4
  N7: J8.pin2, Part1.D5
  N8: J9.pin2, R3.Pin_0, J11.pin2
  N9: J9.pin3, R4.Pin_0, J11.pin3
  N10: J9.pin4, R2.Pin_0, J11.pin4
  N11: J10.pin1, Part1.D7
  N12: J10.pin2, Part1.D8
  N13: J10.pin3, Part1.D9
  N14: Part1.D3, U4.Pin_5
  N15: Part1.D6, J12.pin2
  N16: Part1.D10, U5.Pin_5
  N17: Part1.D11/MOSI, U3.Pin_5
  N18: Part1.D12/MISO, J12.pin3
  N19: Part1.D13/SCK, J12.pin1
  N20: U3.Pin_1, R2.Pin_1, D14.cathode
  N21: U4.Pin_1, R3.Pin_1, D15.cathode
  N22: U5.Pin_1, R4.Pin_1, D16.cathode

custom parts:
  Voltage Regulator - 9V: 9V DC Voltage Regulator
