# Fritzing sketch tachometer_arduino_nano_display_shield (saved by Fritzing 0.8.5b)
circuit board: 9.8763cm x 6.61987cm
breadboards: 1

parts:
  Part2 = Arduino Nano (Rev3.0)
  U1 = Voltage Regulator - 5V [package="TO220 [THT]"]
  J1 = female pin header, 2 pins [form="♀ (female)"]
  J2 = female pin header, 2 pins [form="♀ (female)"]
  J3 = female pin header, 2 pins [form="♀ (female)"]
  J4 = female pin header, 2 pins [form="♀ (female)"]
  J5 = female pin header, 2 pins [form="♀ (female)"]
  LED1 = LED - 5mm [color="Blue (525nm)" package="5 mm [THT]"]
  R1 = Resistor [tolerance=±5% resistance=220 package=THT]

nets:
  GND: Part2.GND, U1.GND, J3.pin1, J5.pin1, J5.pin2, LED1.cathode
  N1: Part2.D4, R1.Pin_1
  N2: Part2.D8, J4.pin1
  N3: Part2.D9, J1.pin1, J1.pin2
  N4: Part2.VIN, U1.input_voltage
  N5: U1.output_voltage, J2.pin1, J2.pin2, J3.pin2
  N6: LED1.anode, R1.Pin_0
