# Fritzing sketch speedo_arduino_uno_shield (saved by Fritzing 0.8.5b)
circuit board: 6.83863cm x 5.30084cm
breadboards: 1

parts:
  J1 = male pin header, 8 pins [form="♂ (male)"]
  J2 = male pin header, 10 pins [form="♂ (male)"]  # not connected
  J3 = male pin header, 6 pins [form="♂ (male)"]  # not connected
  J4 = male pin header, 8 pins [form="♂ (male)"]
  U1 = Voltage Regulator - 9V [package="TO220 [THT]"]
  J5 = male pin header, 2 pins [form="♂ (male)"]
  J6 = male pin header, 3 pins [form="♂ (male)"]
  C1 = Electrolytic Capacitor [capacitance=1µF package="100 mil [THT, electrolytic]"]
  C2 = Ceramic Capacitor [capacitance=100nF package="100 mil [THT, multilayer]"]
  C3 = Ceramic Capacitor [capacitance=100nF package="100 mil [THT, multilayer]"]
  U2 = Optocoupler [package=THT]
  R1 = Resistor [tolerance=±5% resistance=330 package=THT]
  D13 = Rectifier Diode [part_number=1N4001 package="300 mil [THT]"]
  R2 = Resistor [tolerance=±5% resistance=100k package=THT]
  R3 = Resistor [tolerance=±5% resistance=10k package=THT]
  J7 = male pin header, 2 pins [form="♂ (male)"]
  J8 = male pin header, 2 pins [form="♂ (male)"]
  R4 = Resistor [tolerance=±5% resistance=10k package=THT]

nets:
  N1: J1.pin3, U2.Pin_5, R2.Pin_0
  N2: J1.pin5, R3.Pin_0, J7.pin2
  N3: J1.pin6, J8.pin2, R4.Pin_0
  GND: J4.pin2, J4.pin3, U1.GND, J5.pin1, J6.pin1, C1.-, C2.0, C3.0, U2.Pin_2, U2.Pin_4, D13.anode, J7.pin1, J8.pin1
  N4: J4.pin4, R2.Pin_1, R3.Pin_1, R4.Pin_1
  N5: U1.input_voltage, J5.pin2, C1.+, C2.1
  N6: U1.output_voltage, J6.pin3, C3.1
  N7: J6.pin2, R1.Pin_0
  N8: U2.Pin_1, R1.Pin_1, D13.cathode

custom parts:
  Voltage Regulator - 9V: 9V DC Voltage Regulator
