# Fritzing sketch gauges_sensor_shield (saved by Fritzing 0.8.5b)
circuit board: 6.9215cm x 5.33756cm

parts:
  R1 = Resistor [tolerance=±5% resistance=100k package=THT]
  R2 = Resistor [tolerance=±5% resistance=10k package=THT]
  R3 = Resistor [tolerance=±5% resistance=10k package=THT]
  Part1 = Arduino Uno (Rev3)
  R4 = Resistor [tolerance=±5% resistance=10k package=THT]
  R5 = Resistor [tolerance=±5% resistance=220 package=THT]
  R6 = Resistor [tolerance=±5% resistance=10k package=THT]
  R7 = Resistor [tolerance=±5% resistance=220 package=THT]
  R8 = Resistor [tolerance=±5% resistance=10k package=THT]
  R9 = Resistor [tolerance=±5% resistance=220 package=THT]
  R10 = Resistor [tolerance=±5% resistance=10k package=THT]
  R11 = Resistor [tolerance=±5% resistance=220 package=THT]
  R12 = Resistor [tolerance=±5% resistance=10k package=THT]
  R13 = Resistor [tolerance=±5% resistance=220 package=THT]
  J2 = female pin header, 4 pins [form="♀ (female)"]
  J1 = female pin header, 8 pins [form="♀ (female)"]
  J3 = male pin header, 6 pins [form="♂ (male)"]

nets (from the schematic view):
  N1: R1.Pin_0, J1.pin8
  N2: R1.Pin_1, R2.Pin_1, R3.Pin_0
  N3: R2.Pin_0, Part1.GND, J2.pin1
  N4: R3.Pin_1, Part1.A0
  N5: Part1.A1, R4.Pin_0
  N6: Part1.A2, R6.Pin_0
  N7: Part1.A3, R8.Pin_0
  N8: Part1.A4/SDA, R10.Pin_0
  N9: Part1.A5/SCL, R12.Pin_0
  N10: Part1.D8, J2.pin2
  N11: Part1.D9_PWM, J2.pin3
  N12: Part1.D10_PWM/SS, J2.pin4
  N13: Part1.D2, J3.pin1
  N14: Part1.D3_PWM, J3.pin2
  N15: Part1.D4, J3.pin3
  N16: Part1.D5_PWM, J3.pin4
  N17: Part1.D6_PWM, J3.pin5
  N18: Part1.D7, J3.pin6
  N19: Part1.VIN, J1.pin1
  N20: R4.Pin_1, R5.Pin_1, J1.pin7
  N21: R5.Pin_0, R7.Pin_0, R9.Pin_0, R11.Pin_0, R13.Pin_0, J1.pin2
  N22: R6.Pin_1, R7.Pin_1, J1.pin6
  N23: R8.Pin_1, R9.Pin_1, J1.pin5
  N24: R10.Pin_1, R11.Pin_1, J1.pin4
  N25: R12.Pin_1, R13.Pin_1, J1.pin3
