# Fritzing sketch powersupply (saved by Fritzing 0.8.5b)
circuit board: 7.85562cm x 3.46343cm
perfboards: 1

parts:
  J2 = Screw terminal - 2 pins [package=THT]
  C1 = Electrolytic Capacitor [capacitance=10µF voltage=50V package="100 mil [THT, electrolytic]"]
  C2 = Electrolytic Capacitor [capacitance=10µF voltage=50V package="100 mil [THT, electrolytic]"]
  C3 = Ceramic Capacitor [capacitance=100nF package="100 mil [THT, multilayer]"]
  C4 = Ceramic Capacitor [capacitance=100nF package="100 mil [THT, multilayer]"]
  C5 = Ceramic Capacitor [capacitance=100nF package="100 mil [THT, multilayer]"]
  C6 = Ceramic Capacitor [capacitance=100nF package="100 mil [THT, multilayer]"]
  J1 = screw terminal, 2 pins
  C8 = Ceramic Capacitor [capacitance=100nF package="100 mil [THT, multilayer]"]
  C9 = Ceramic Capacitor [capacitance=100nF package="100 mil [THT, multilayer]"]
  U1 = Voltage Regulator - 5V [package="TO220 [THT]"]
  J3 = Screw terminal - 2 pins [package=THT]
  J4 = Screw terminal - 2 pins [package=THT]
  J5 = Screw terminal - 2 pins [package=THT]
  J6 = female pin header, 2 pins [form="♀ (female)"]
  J7 = female pin header, 2 pins [form="♀ (female)"]
  J8 = female pin header, 2 pins [form="♀ (female)"]
  U4 = Voltage Regulator - 9V [package="TO220 [THT]"]
  U3 = Voltage Regulator - 5V [package="TO220 [THT]"]

nets:
  GND: J2.pin1, C1.-, C2.-, C3.0, C4.0, C5.0, C6.0, J1.pin1, C8.0, C9.0, U1.GND, J3.pin2, J4.pin2, J5.pin2, J6.pin2, J7.pin2, J8.pin2, U4.GND, U3.GND
  N1: J2.pin2, C2.+, C5.1, U4.input_voltage
  N2: C1.+, C3.1, J1.pin2, C9.1, U1.input_voltage, U3.input_voltage
  N3: C4.1, U1.output_voltage, J4.pin1, J7.pin1
  N4: C6.1, J3.pin1, J6.pin1, U4.output_voltage
  N5: C8.1, J5.pin1, J8.pin1, U3.output_voltage

custom parts:
  Voltage Regulator - 9V: 9V DC Voltage Regulator
