# Fritzing sketch sensor_input_board (saved by Fritzing 0.8.5b)
circuit board: 6.6cm x 8cm
breadboards: 1

parts:
  R1 = Resistor [tolerance=±5% resistance=100 package=THT]
  J1 = female pin header, 2 pins [form="♀ (female)"]
  J2 = female pin header, 2 pins [form="♀ (female)"]
  R2 = Resistor [tolerance=±5% resistance=10k package=THT]
  D1 = Schottky Diode [part_number=1N5817 package="300 mil [THT]"]
  D2 = Schottky Diode [part_number=1N5817 package="300 mil [THT]"]
  R3 = Resistor [tolerance=±5% resistance=2.2k package=THT]
  J5 = female pin header, 2 pins [form="♀ (female)"]
  D4 = Schottky Diode [part_number=1N5817 package="300 mil [THT]"]
  D3 = Schottky Diode [part_number=1N5817 package="300 mil [THT]"]
  R4 = Resistor [tolerance=±5% resistance=10k package=THT]
  R5 = Resistor [tolerance=±5% resistance=2.2k package=THT]
  J6 = female pin header, 2 pins [form="♀ (female)"]
  D6 = Schottky Diode [part_number=1N5817 package="300 mil [THT]"]
  D5 = Schottky Diode [part_number=1N5817 package="300 mil [THT]"]
  R6 = Resistor [tolerance=±5% resistance=10k package=THT]
  R7 = Resistor [tolerance=±5% resistance=15k package=THT]
  J7 = female pin header, 2 pins [form="♀ (female)"]
  D7 = Schottky Diode [part_number=1N5817 package="300 mil [THT]"]
  D8 = Schottky Diode [part_number=1N5817 package="300 mil [THT]"]
  R8 = Resistor [tolerance=±5% resistance=10k package=THT]
  R9 = Resistor [tolerance=±5% resistance=10k package=THT]
  C4 = Ceramic Capacitor [capacitance=0.1µF voltage=20V package="100 mil [THT, multilayer]"]
  C3 = Ceramic Capacitor [capacitance=0.1µF voltage=20V package="100 mil [THT, multilayer]"]
  C2 = Ceramic Capacitor [capacitance=0.1µF voltage=20V package="100 mil [THT, multilayer]"]
  C1 = Ceramic Capacitor [capacitance=0.1µF voltage=20V package="100 mil [THT, multilayer]"]
  J9 = female pin header, 2 pins [form="♀ (female)"]  # not connected
  J8 = female pin header, 2 pins [form="♀ (female)"]  # not connected
  J3 = rounded female pin header, 6 pins [form="♀ (female rounded)"]

nets:
  N1: R1.Pin_0, J1.pin2, D1.cathode, R3.Pin_0, D3.cathode, R5.Pin_0, D5.cathode, R7.Pin_0, D7.cathode
  N2: R1.Pin_1, J2.pin2, R2.Pin_0
  GND: J1.pin1, D2.anode, D4.anode, D6.anode, D8.anode, R9.Pin_1, C4.0, C3.0, C2.0, C1.0
  N3: R2.Pin_1, D1.anode, D2.cathode, C1.1, J3.pin1
  N4: R3.Pin_1, J5.pin2, R4.Pin_0
  N5: D4.cathode, D3.anode, R4.Pin_1, C2.1, J3.pin2
  N6: R5.Pin_1, J6.pin2, R6.Pin_0
  N7: D6.cathode, D5.anode, R6.Pin_1, C3.1, J3.pin3
  N8: R7.Pin_1, J7.pin2, R8.Pin_0, R9.Pin_0
  N9: D7.anode, D8.cathode, R8.Pin_1, C4.1, J3.pin4
